// Logisim project lab3a.circ as structural Verilog: 4 circuits, main circuit mux2to1
module mux2to1 (
  input  [3:0] in_1,
  input  [3:0] in_2,
  input  S,
  output [3:0] out_4
);

  origin2to1 origin2to1_1 (.X(in_1[0]), .s(S), .in_3(in_2[0]), .m(out_4[0]));
  origin2to1 origin2to1_2 (.X(in_1[1]), .s(S), .in_3(in_2[1]), .m(out_4[1]));
  origin2to1 origin2to1_3 (.X(in_1[2]), .s(S), .in_3(in_2[2]), .m(out_4[2]));
  origin2to1 origin2to1_4 (.X(in_1[3]), .s(S), .in_3(in_2[3]), .m(out_4[3]));

  // Notes on the sheet:
  //   X
  //   Y
  //   M
endmodule

module origin2to1 (
  input  X,
  input  s,
  input  in_3,
  output m
);

  wire and_1_out, and_2_out, not_1_out;

  not not_1 (not_1_out, s);
  and and_1 (and_1_out, X, not_1_out);
  and and_2 (and_2_out, s, in_3);
  or or_1 (m, and_1_out, and_2_out);

  // Notes on the sheet:
  //   y
endmodule

module mux2to1mux (
  input  [3:0] in_1,
  input  [3:0] in_2,
  input  in_3,
  output [3:0] out_4
);

  Multiplexer multiplexer_1 (.in0(in_1[3]), .in1(in_2[3]), .out(out_4[3]), .sel(in_3));
  Multiplexer multiplexer_2 (.in0(in_1[0]), .in1(in_2[0]), .out(out_4[0]), .sel(in_3));
  Multiplexer multiplexer_3 (.in0(in_1[1]), .in1(in_2[1]), .out(out_4[1]), .sel(in_3));
  Multiplexer multiplexer_4 (.in0(in_1[2]), .in1(in_2[2]), .out(out_4[2]), .sel(in_3));
endmodule

module mux2to1plus (
  input  [3:0] X,
  input  S,
  input  [3:0] Y,
  output [3:0] M
);

  wire [3:0] and_1_out, and_2_out, not_1_out;

  assign not_1_out = ~{4{S}};  // NOT_Gate not_1, 4 bits wide
  assign and_1_out = X & not_1_out;  // AND_Gate and_1, 4 bits wide
  assign and_2_out = {4{S}} & Y;  // AND_Gate and_2, 4 bits wide
  assign M = and_1_out | and_2_out;  // OR_Gate or_1, 4 bits wide
endmodule
