// Logisim project lab3b.circ as structural Verilog: 2 circuits, main circuit fa
module fa (
  input  in_1,
  input  in_2,
  input  in_3,
  output out_4,
  output out_5
);

  wire and_1_out, and_2_out, xor_1_out;

  and and_1 (and_1_out, in_3, in_2);
  xor xor_1 (xor_1_out, in_2, in_3);
  and and_2 (and_2_out, xor_1_out, in_1);
  or or_1 (out_5, and_2_out, and_1_out);
  xor xor_2 (out_4, in_1, xor_1_out);

  // Notes on the sheet:
  //   x
  //   y
  //   C in
  //   S
  //   C out
endmodule

module adder4 (
  input  [3:0] in_1,
  input  Sub,
  input  [3:0] in_3,
  output [3:0] S,
  output C
);

  wire fa_1_out_5, fa_2_out_5, fa_3_out_5, xor_1_out, xor_2_out, xor_3_out, xor_4_out;

  xor xor_1 (xor_1_out, Sub, in_3[0]);
  xor xor_2 (xor_2_out, Sub, in_3[1]);
  fa fa_1 (.in_1(Sub), .in_2(in_1[0]), .in_3(xor_1_out), .out_4(S[0]), .out_5(fa_1_out_5));
  fa fa_2 (.in_1(fa_1_out_5), .in_2(in_1[1]), .in_3(xor_2_out), .out_4(S[1]), .out_5(fa_2_out_5));
  xor xor_3 (xor_3_out, Sub, in_3[2]);
  fa fa_3 (.in_1(fa_2_out_5), .in_2(in_1[2]), .in_3(xor_3_out), .out_4(S[2]), .out_5(fa_3_out_5));
  xor xor_4 (xor_4_out, Sub, in_3[3]);
  fa fa_4 (.in_1(fa_3_out_5), .in_2(in_1[3]), .in_3(xor_4_out), .out_4(S[3]), .out_5(C));

  // Notes on the sheet:
  //   X
  //   Y
endmodule
