// Logisim project lab3c.circ as structural Verilog: 2 circuits, main circuit main
module main (
  output [3:0] out_1
);

  wire [1:0] dipswitch_3_sw2;
  wire [3:0] dipswitch_1_sw4, dipswitch_2_sw4;

  DipSwitch #(.number(4)) dipswitch_1 (
    .sw1(dipswitch_1_sw4[3]), .sw2(dipswitch_1_sw4[2]), .sw3(dipswitch_1_sw4[1]), .sw4(dipswitch_1_sw4[0]));
  DipSwitch #(.number(4)) dipswitch_2 (
    .sw1(dipswitch_2_sw4[3]), .sw2(dipswitch_2_sw4[2]), .sw3(dipswitch_2_sw4[2]), .sw4(dipswitch_2_sw4[0]));
  DipSwitch #(.number(2)) dipswitch_3 (.sw1(dipswitch_3_sw2[1]), .sw2(dipswitch_3_sw2[0]));
  LED led_1 (.in(dipswitch_3_sw2[0]));
  LED led_2 (.in(dipswitch_3_sw2[1]));
  Hex_Digit_Display hex_digit_display_1 (.value(dipswitch_1_sw4));  // open: dp
  Hex_Digit_Display hex_digit_display_2 (.value({dipswitch_2_sw4[3:2], dipswitch_2_sw4[2], dipswitch_2_sw4[0]}));  // open: dp
  ALU alu_1 (
    .in_1(dipswitch_1_sw4), .in_2({dipswitch_2_sw4[3:2], dipswitch_2_sw4[2], dipswitch_2_sw4[0]}),
    .in_3(dipswitch_3_sw2), .out_4(out_1));
  Hex_Digit_Display hex_digit_display_3 (.value(out_1));  // open: dp

  // Notes on the sheet:
  //   X
  //   Y
  //   func
  //   Z
endmodule

module ALU (
  input  [3:0] in_1,
  input  [3:0] in_2,
  input  [1:0] in_3,
  output [3:0] out_4
);

  wire adder4_1_c;
  wire [3:0] adder4_1_s, and_1_out, mux2to1_1_out_4, or_1_out;

  assign or_1_out = in_1 | in_2;  // OR_Gate or_1, 4 bits wide
  assign and_1_out = in_1 & in_2;  // AND_Gate and_1, 4 bits wide
  adder4 adder4_1 (.in_1(in_1), .Sub(in_3[0]), .in_3(in_2), .S(adder4_1_s), .C(adder4_1_c));
  mux2to1 mux2to1_1 (.in_1(and_1_out), .in_2(or_1_out), .S(in_3[0]), .out_4(mux2to1_1_out_4));
  mux2to1 mux2to1_2 (.in_1(adder4_1_s), .in_2(mux2to1_1_out_4), .S(in_3[1]), .out_4(out_4));
  // also tied to GND on the sheet: adder4_1_c

  // Notes on the sheet:
  //   X
  //   Y
  //   func
  //   Z
endmodule
