// Logisim project Part2.circ as structural Verilog: 5 circuits, main circuit main
module main (
  input  S,
  input  Clock,
  input  R,
  output Q,
  output notQ
);

  wire and_1_out, and_2_out;

  and and_1 (and_1_out, S, Clock);
  and and_2 (and_2_out, Clock, R);
  nor nor_1 (Q, and_1_out, notQ);
  nor nor_2 (notQ, Q, and_2_out);

  // Notes on the sheet:
  //   S
  //   Clock
  //   R
endmodule

module DLatch1 (
  input  D,
  input  C,
  output notQ,
  output Q
);

  wire nand_1_out, nand_2_out, not_1_out;

  not not_1 (not_1_out, D);
  nand nand_1 (nand_1_out, D, C);
  nand nand_2 (nand_2_out, C, not_1_out);
  nor nor_1 (notQ, nand_1_out, Q);
  nor nor_2 (Q, notQ, nand_2_out);
endmodule

module SR (
  input  in_1,
  input  in_2,
  output out_3,
  output out_4
);

  nor nor_1 (out_3, in_1, out_4);
  nor nor_2 (out_4, out_3, in_2);
endmodule

module DLatch (
  input  D,
  input  C,
  output Q,
  output notQ
);

  wire not_1_out;

  not not_1 (not_1_out, D);
  main main_1 (.S(D), .Clock(C), .R(not_1_out), .Q(Q), .notQ(notQ));
endmodule

module positive (
  input  D,
  input  Clock,
  output Q,
  output notQ
);

  wire dlatch_1_notq, dlatch_1_q, not_1_out, not_2_out;

  not not_1 (not_1_out, Clock);
  DLatch dlatch_1 (.D(D), .C(not_1_out), .Q(dlatch_1_q), .notQ(dlatch_1_notq));
  not not_2 (not_2_out, not_1_out);
  DLatch dlatch_2 (.D(dlatch_1_q), .C(not_2_out), .Q(Q), .notQ(notQ));
  // also tied to GND on the sheet: dlatch_1_notq
endmodule
