// Logisim project lab1_namelogic.circ as structural Verilog: 9 circuits, main circuit main
module main (
  input  A,
  input  B,
  input  C
);

  wire buffer_1_out, buffer_2_out, buffer_3_out, namelogic_1_out_4, namelogic_1_out_5, namelogic_1_out_6,
       namelogic_1_out_10, namelogic_1_s1, namelogic_1_s2, namelogic_1_s3;

  buf buffer_1 (buffer_1_out, A);
  buf buffer_2 (buffer_2_out, B);
  buf buffer_3 (buffer_3_out, C);
  namelogic namelogic_1 (
    .in_1(buffer_1_out), .in_2(buffer_2_out), .B(buffer_3_out), .out_4(namelogic_1_out_4),
    .out_5(namelogic_1_out_5), .out_6(namelogic_1_out_6), .S3(namelogic_1_s3), .S2(namelogic_1_s2),
    .S1(namelogic_1_s1), .out_10(namelogic_1_out_10));
  _7_Segment_Display u_7_segment_display_1 (
    .g(namelogic_1_out_4), .f(namelogic_1_out_5), .a(namelogic_1_out_10), .b(namelogic_1_s1),
    .e(namelogic_1_out_6), .d(namelogic_1_s3), .c(namelogic_1_s2));  // open: dp
endmodule

module namelogic (
  input  in_1,
  input  in_2,
  input  B,
  output out_4,
  output out_5,
  output out_6,
  output S3,
  output S2,
  output S1,
  output out_10
);

  S6 s6_1 (.A(in_1), .C(in_2), .B(B), .S6(out_4));
  S5 s5_1 (.A(in_1), .B(in_2), .C(B), .S5(out_5));
  S4 s4_1 (.A(in_1), .B(in_2), .C(B), .S4(out_6));
  S3 s3_1 (.in_1(in_1), .B(in_2), .C(B), .S3(S3));
  S2 s2_1 (.A(in_1), .B(in_2), .C(B), .S2(S2));
  S1 s1_1 (.A(in_1), .B(in_2), .C(B), .S1(S1));
  S0 s0_1 (.A(in_1), .B(in_2), .C(B), .S0(out_10));

  // Notes on the sheet:
  //   A
  //   C
  //   S5
  //   S4
  //   S0
  //   S6
endmodule

module S6 (
  input  A,
  input  C,
  input  B,
  output S6
);

  wire and_1_out, and_2_out, and_3_out, not_1_out, not_2_out, not_3_out, or_1_out;

  not not_1 (not_1_out, A);
  not not_2 (not_2_out, B);
  not not_3 (not_3_out, C);
  and and_1 (and_1_out, not_1_out, C);
  and and_2 (and_2_out, A, not_2_out);
  and and_3 (and_3_out, B, not_3_out);
  or or_1 (or_1_out, and_2_out, and_3_out);
  or or_2 (S6, and_1_out, or_1_out);
endmodule

module S5 (
  input  A,
  input  B,
  input  C,
  output S5
);

  wire and_1_out, not_1_out, not_2_out, not_3_out;

  not not_1 (not_1_out, A);
  not not_2 (not_2_out, B);
  not not_3 (not_3_out, C);
  and and_1 (and_1_out, not_1_out, not_2_out);
  or or_1 (S5, and_1_out, not_3_out);
endmodule

module S4 (
  input  A,
  input  B,
  input  C,
  output S4
);

  wire and_1_out, and_2_out, not_1_out, not_2_out, not_3_out, or_1_out;

  not not_1 (not_1_out, C);
  and and_1 (and_1_out, B, not_1_out);
  not not_2 (not_2_out, B);
  not not_3 (not_3_out, A);
  and and_2 (and_2_out, not_2_out, C);
  or or_1 (or_1_out, and_1_out, and_2_out);
  or or_2 (S4, not_3_out, or_1_out);
endmodule

module S3 (
  input  in_1,
  input  B,
  input  C,
  output S3
);

  wire and_1_out, and_2_out, and_3_out, not_1_out, not_2_out, or_1_out;

  not not_1 (not_1_out, B);
  not not_2 (not_2_out, C);
  and and_1 (and_1_out, in_1, not_1_out);
  and and_2 (and_2_out, in_1, not_2_out);
  and and_3 (and_3_out, not_1_out, not_2_out);
  or or_1 (or_1_out, and_2_out, and_3_out);
  or or_2 (S3, and_1_out, or_1_out);

  // Notes on the sheet:
  //   A
endmodule

module S2 (
  input  A,
  input  B,
  input  C,
  output S2
);

  wire and_1_out, and_2_out, and_3_out, and_4_out, not_1_out, not_2_out, not_3_out, or_1_out;

  not not_1 (not_1_out, B);
  not not_2 (not_2_out, A);
  and and_1 (and_1_out, A, not_1_out);
  not not_3 (not_3_out, C);
  and and_2 (and_2_out, not_2_out, B);
  and and_3 (and_3_out, not_2_out, C);
  and and_4 (and_4_out, and_1_out, not_3_out);
  or or_1 (or_1_out, and_2_out, and_3_out);
  or or_2 (S2, and_4_out, or_1_out);
endmodule

module S1 (
  input  A,
  input  B,
  input  C,
  output S1
);

  wire and_1_out, and_2_out, and_3_out, not_1_out, not_2_out, not_3_out;

  not not_1 (not_1_out, A);
  not not_2 (not_2_out, C);
  not not_3 (not_3_out, B);
  and and_1 (and_1_out, not_1_out, B);
  and and_2 (and_2_out, A, not_3_out);
  and and_3 (and_3_out, and_1_out, not_2_out);
  or or_1 (S1, and_3_out, and_2_out);
endmodule

module S0 (
  input  A,
  input  B,
  input  C,
  output S0
);

  wire and_1_out, not_1_out, not_2_out;

  not not_1 (not_1_out, B);
  not not_2 (not_2_out, C);
  and and_1 (and_1_out, A, not_1_out);
  or or_1 (S0, and_1_out, not_2_out);
endmodule
