// Logisim project part1.circ as structural Verilog: 3 circuits, main circuit statelogic
module statelogic (
  input  F1,
  input  F0,
  input  A,
  input  B,
  output newF1,
  output newF0
);

  wire and_1_out, and_2_out, and_3_out, and_4_out, and_5_out, and_6_out, and_7_out, and_8_out, and_9_out,
       and_10_out, not_1_out, not_2_out, not_3_out, not_4_out, or_1_out, or_3_out, or_4_out;

  not not_1 (not_1_out, F1);
  and and_1 (and_1_out, A, B);
  not not_2 (not_2_out, B);
  and and_2 (and_2_out, A, not_2_out);
  and and_3 (and_3_out, B, F0);
  not not_3 (not_3_out, A);
  not not_4 (not_4_out, B);
  and and_4 (and_4_out, and_3_out, not_1_out);
  and and_5 (and_5_out, not_3_out, not_4_out);
  or or_1 (or_1_out, and_1_out, and_2_out);
  and and_6 (and_6_out, F1, F0);
  and and_7 (and_7_out, F0, and_5_out);
  and and_8 (and_8_out, F0, B);
  and and_9 (and_9_out, not_3_out, not_4_out);
  or or_2 (newF0, or_1_out, and_4_out);
  and and_10 (and_10_out, and_9_out, F1);
  or or_3 (or_3_out, and_6_out, and_7_out);
  or or_4 (or_4_out, and_8_out, and_10_out);
  or or_5 (newF1, or_3_out, or_4_out);
endmodule

module outputlogic (
  input  F1,
  input  F0,
  output R,
  output L
);

  wire not_1_out, not_2_out;

  not not_1 (not_1_out, F1);
  not not_2 (not_2_out, F0);
  and and_1 (R, not_1_out, F0);
  and and_2 (L, F1, not_2_out);
endmodule

module total (
);

  wire AB_sw1, AB_sw2, CLK_out, F0_q, F1_q, outputlogic_1_l, outputlogic_1_r, reset_out, statelogic_1_newf0,
       statelogic_1_newf1;

  Button CLK (.out(CLK_out));
  Button reset (.out(reset_out));
  D_Flip_Flop F1 (.D(statelogic_1_newf1), .clk(CLK_out), .Q(F1_q), .reset(reset_out));  // open: Qn, preset
  D_Flip_Flop F0 (.D(statelogic_1_newf0), .clk(CLK_out), .Q(F0_q), .reset(reset_out));  // open: Qn, preset
  DipSwitch #(.number(2)) AB (.sw1(AB_sw1), .sw2(AB_sw2));
  statelogic statelogic_1 (
    .F1(F1_q), .F0(F0_q), .A(AB_sw1), .B(AB_sw2), .newF1(statelogic_1_newf1), .newF0(statelogic_1_newf0));
  outputlogic outputlogic_1 (.F1(F1_q), .F0(F0_q), .R(outputlogic_1_r), .L(outputlogic_1_l));
  LED R (.in(outputlogic_1_r));
  LED L (.in(outputlogic_1_l));
endmodule
