// Logisim project lab04_base.circ as structural Verilog: 5 circuits, main circuit register_file
module register_file (
  input  clear,
  input  [1:0] read_reg,
  input  [7:0] data_write,
  input  [1:0] write_reg,
  input  write_enable,
  input  clock,
  input  reset,
  output [7:0] data_read
);

  wire and_1_out, and_2_out, and_3_out, and_4_out, decoder_1_out0, decoder_1_out1, decoder_1_out2,
       decoder_1_out3;
  wire [7:0] multiplexer_1_out, register_1_q, register_2_q, register_3_q, register_4_q;

  Decoder #(.select(2)) decoder_1 (
    .out0(decoder_1_out0), .out1(decoder_1_out1), .out2(decoder_1_out2), .out3(decoder_1_out3),
    .sel(write_reg));  // open: en
  Multiplexer #(.width(8)) multiplexer_1 (.in0(data_write), .in1({8{1'b0}}), .out(multiplexer_1_out), .sel(clear));
  and and_1 (and_1_out, decoder_1_out0, write_enable);
  and and_2 (and_2_out, decoder_1_out1, write_enable);
  and and_3 (and_3_out, decoder_1_out2, write_enable);
  and and_4 (and_4_out, decoder_1_out3, write_enable);
  Register register_1 (.D(multiplexer_1_out), .en(and_1_out), .clk(clock), .Q(register_1_q), .clr(reset));
  Register register_2 (.D(multiplexer_1_out), .en(and_2_out), .clk(clock), .Q(register_2_q), .clr(reset));
  Register register_3 (.D(multiplexer_1_out), .en(and_3_out), .clk(clock), .Q(register_3_q), .clr(reset));
  Register register_4 (.D(multiplexer_1_out), .en(and_4_out), .clk(clock), .Q(register_4_q), .clr(reset));
  Multiplexer #(.select(2), .width(8)) multiplexer_2 (
    .in0(register_1_q), .in1(register_2_q), .in2(register_3_q), .in3(register_4_q), .out(data_read),
    .sel(read_reg));
endmodule

module alu (
  input  [7:0] A,
  input  [7:0] B,
  input  op,
  output [7:0] data_out
);

  wire [7:0] adder_1_out, multiplier_1_out;

  Multiplier multiplier_1 (.a(A), .b(B), .out(multiplier_1_out));  // open: cin, cout
  Adder adder_1 (.a(A), .b(B), .out(adder_1_out));  // open: cin, cout
  Multiplexer #(.width(8)) multiplexer_1 (.in0(multiplier_1_out), .in1(adder_1_out), .out(data_out), .sel(op));
endmodule

module instr_decoder (
  input  [7:0] instr,
  output [1:0] imm,
  output [1:0] write_reg,
  output [1:0] read_reg,
  output reg_clear,
  output alu_op,
  output write_en
);

  wire and_1_out, and_2_out, not_1_out, not_2_out, not_3_out;

  not not_1 (not_1_out, instr[6]);
  not not_2 (not_2_out, instr[7]);
  and and_1 (and_1_out, not_1_out, instr[7]);
  and and_2 (and_2_out, instr[6], not_2_out);
  and and_3 (reg_clear, instr[6], instr[7]);
  not not_3 (not_3_out, and_2_out);
  and and_4 (alu_op, and_1_out, not_3_out);
  or or_1 (write_en, and_1_out, and_2_out);

  assign imm = instr[1:0];
  assign read_reg = instr[5:4];
  assign write_reg = instr[3:2];
endmodule

module script (
  input  in_1,
  input  in_2,
  input  in_3,
  input  in_4,
  output out_5,
  output out_6,
  output out_7,
  output out_8
);

  wire decoder_1_out0, decoder_1_out1;

  Decoder decoder_1 (.out0(decoder_1_out0), .out1(decoder_1_out1), .sel(in_2));  // open: en
  Decoder decoder_2 (.out0(out_7), .out1(out_8), .sel(in_4), .en(in_3));
  and and_1 (out_5, in_1, decoder_1_out0);
  and and_2 (out_6, in_1, decoder_1_out1);
endmodule

module main (
  input  [7:0] in_1,
  input  in_2,
  output [7:0] out_3
);

  wire clock_1_out, instr_decoder_1_alu_op, instr_decoder_1_reg_clear, instr_decoder_1_write_en;
  wire [1:0] instr_decoder_1_imm, instr_decoder_1_read_reg, instr_decoder_1_write_reg;
  wire [7:0] bit_extender_1_out, register_file_1_data_read;

  Clock clock_1 (.out(clock_1_out));
  instr_decoder instr_decoder_1 (
    .instr(in_1), .imm(instr_decoder_1_imm), .write_reg(instr_decoder_1_write_reg),
    .read_reg(instr_decoder_1_read_reg), .reg_clear(instr_decoder_1_reg_clear),
    .alu_op(instr_decoder_1_alu_op), .write_en(instr_decoder_1_write_en));
  assign bit_extender_1_out = {{6{1'b0}}, instr_decoder_1_imm};  // Bit_Extender bit_extender_1
  register_file register_file_1 (
    .clear(instr_decoder_1_reg_clear), .read_reg(instr_decoder_1_read_reg), .data_write(out_3),
    .write_reg(instr_decoder_1_write_reg), .write_enable(instr_decoder_1_write_en), .clock(clock_1_out),
    .reset(in_2), .data_read(register_file_1_data_read));
  alu alu_1 (.A(bit_extender_1_out), .B(register_file_1_data_read), .op(instr_decoder_1_alu_op), .data_out(out_3));
endmodule
